# Fritzing sketch Montage (saved by Fritzing 0.9.8b)
breadboards: 1

parts:
  U1 = NodeMCU V1.0
  M1 = MAX7219 8x8 single Led Matrix Module
  DHT1 = DHT11 Humitidy and Temperature Sensor
  R1 = Photocell (LDR) [package=THT]
  R3 = Resistor [tolerance=±5% resistance=10k package="0805 [SMD]"]
  R2 = Resistor [tolerance=±5% resistance=10k package="0805 [SMD]"]

nets:
  N1: U1.D3, DHT1.DATA, R3.Pin_1
  N2: U1.D4, M1.I-GND-1, M1.O-GND-1
  3V3: U1.3V3, M1.I-CLK-1, DHT1.VDD, R1.pin_1, R3.Pin_0
  GND: U1.GND, M1.I-CS-1, M1.O-CS-1, DHT1.GND, R2.Pin_1
  N3: U1.D6, M1.I-VCC-1, M1.O-VCC-1
  N4: U1.D7, M1.I-DIN-1
  N5: U1.A0, R1.pin_0, R2.Pin_0

notes:
  CLK
  CS
  DIN
  GND
  VCC

custom parts:
  NodeMCU V1.0: ESP8266 based NodeMCU
  MAX7219 8x8 single Led Matrix Module: Description: MAX7219 8x8 LedMatrix single Red Module Dimensions: 32x32mm Documents:
  DHT11 Humitidy and Temperature Sensor: DHT11 Humidity and Temperature Sensor
